# Fritzing sketch temperature (saved by Fritzing 0.9.2b)
breadboards: 1

parts:
  Part1 = Arduino Mega ADK (Rev3)
  U1 = 7-SEGMENT-4DIGIT [package=7-segment-4digit-youngsun]
  R1 = Resistor [tolerance=±5% resistance=220 package=THT]
  R3 = Resistor [tolerance=±5% resistance=220 package=THT]
  R4 = Resistor [tolerance=±5% resistance=220 package=THT]
  R5 = Resistor [tolerance=±5% resistance=220 package=THT]

nets:
  N1: Part1.D13_PWM, R1.Pin_1
  N2: Part1.D12_PWM, R5.Pin_1
  N3: Part1.D11_PWM, U1.5
  N4: Part1.D10_PWM, U1.4
  N5: Part1.D9_PWM, U1.3
  N6: Part1.D8_PWM, U1.2
  N7: Part1.D2_PWM, U1.15
  N8: Part1.D3_PWM, U1.14
  N9: Part1.D4_PWM, U1.13
  N10: Part1.D5_PWM, R3.Pin_1
  N11: Part1.D6_PWM, R4.Pin_1
  N12: Part1.D7_PWM, U1.1
  N13: U1.6, R5.Pin_0
  N14: U1.11, R4.Pin_0
  N15: U1.16, R1.Pin_0
